# Fritzing sketch hbridge (saved by Fritzing 0.9.6b)
breadboards: 1

parts:
  IC1 = H-Bridge [package=THT]
  VCC1 = 4 x AAA Battery Mount
  M1 = DC Motor
  D1 = Diode [part_number=1n4001 package=diode-1n4001]
  R1 = Resistor [tolerance=±5% resistance=22k package="2010 [SMD]"]
  Mod1 = MSP-EXP432P401R_EagleCAD
  R2 = Resistor [tolerance=±5% resistance=33k package="2010 [SMD]"]
  D2 = Diode [part_number=1n5819 package=diode-1n4001]
  D3 = Diode [part_number=1n5819 package=diode-1n4001]
  D4 = Diode [part_number=1n5819 package=diode-1n4001]
  D5 = Diode [part_number=1n5819 package=diode-1n4001]
  C1 = Capacitor [package=cap-pth-small2]
  C2 = Capacitor [package=cap-pth-small2]
  C3 = Capacitor Polarized [package=panasonic_d]

nets:
  N1: IC1.1_2EN, R1.Pin_0, Mod1.P2.4
  N2: IC1.1A, Mod1.P2.6
  N3: IC1.1Y, M1.pin_1, D3.C
  GND1: IC1.GND1, IC1.GND2, IC1.GND3, IC1.GND4, VCC1.-, R1.Pin_1, Mod1.GND, R2.Pin_0, C1.1, C2.1, C3.-
  N4: IC1.2Y, M1.pin_2, D5.C
  N5: IC1.2A, Mod1.P2.7
  N6: IC1.VCC2, VCC1.+, D2.C, D4.C, C2.2, C3.+
  N7: IC1.3_4EN, R2.Pin_1
  N8: IC1.VCC1, D1.C, C1.2

custom parts:
  MSP-EXP432P401R_EagleCAD: TI Launch pad MSP-EXP432P401R development board.
